// Logisim project lab2.5.circ as structural Verilog: 1 circuit, main circuit main
module main (
  input  [7:0] DataIn,
  input  [2:0] shamt,
  input  L_R,
  input  A_L,
  output [7:0] DataOut
);

  wire [0:0] and_2_out;
  wire [1:0] and_4_out;
  wire [3:0] and_7_out;
  wire [7:0] multiplexer_1_out, multiplexer_2_out;
  wire [7:7] and_1_out, and_3_out, and_6_out;

  and and_1 (and_1_out[7], A_L, DataIn[7]);
  and and_2 (and_2_out[0], DataIn[7], A_L);
  Multiplexer #(.select(2), .width(8), .enable("false")) multiplexer_1 (
    .in0(DataIn), .in1({and_1_out[7], DataIn[7:1]}), .in2(DataIn), .in3({DataIn[6:0], and_2_out[0]}),
    .out(multiplexer_1_out), .sel({L_R, shamt[0]}));
  and and_3 (and_3_out[7], A_L, multiplexer_1_out[7]);
  and and_4 (and_4_out[0], multiplexer_1_out[6], A_L);
  and and_5 (and_4_out[1], multiplexer_1_out[7], A_L);
  Multiplexer #(.select(2), .width(8), .enable("false")) multiplexer_2 (
    .in0(multiplexer_1_out), .in1({{2{and_3_out[7]}}, multiplexer_1_out[7:2]}), .in2(multiplexer_1_out),
    .in3({multiplexer_1_out[5:0], and_4_out}), .out(multiplexer_2_out), .sel({L_R, shamt[1]}));
  and and_6 (and_6_out[7], A_L, multiplexer_2_out[7]);
  and and_7 (and_7_out[0], multiplexer_2_out[4], A_L);
  and and_8 (and_7_out[1], multiplexer_2_out[5], A_L);
  and and_9 (and_7_out[2], multiplexer_2_out[6], A_L);
  and and_10 (and_7_out[3], multiplexer_2_out[7], A_L);
  Multiplexer #(.select(2), .width(8), .enable("false")) multiplexer_3 (
    .in0(multiplexer_2_out), .in1({{4{and_6_out[7]}}, multiplexer_2_out[7:4]}), .in2(multiplexer_2_out),
    .in3({multiplexer_2_out[3:0], and_7_out}), .out(DataOut), .sel({L_R, shamt[2]}));

  // Other names for the same wires on the sheet: Din[7:0] = DataIn; Left_Right = L_R; Arth_Logic = A_L;
  //   Dout[7:0] = DataOut

  // Notes on the sheet:
  //   L/R,A/L: 00逻辑右移，01算术右移，10逻辑左移，11：循环左移
  //   输入引脚
  //   请勿修改引脚名称、电路名称及电路封装外观
  //   提示：使用多路选择器级联实现8位桶形移位器，禁止直接使用移位器组件。
  //   输出引脚
endmodule
