// Logisim project lab3.5.circ as structural Verilog: 1 circuit, main circuit main
module main (
  input  CLK,
  input  LD,
  input  [3:0] HH1,
  input  [3:0] HH0,
  input  [3:0] MM1,
  input  [3:0] MM0,
  input  [3:0] SS1,
  input  [3:0] SS0,
  output [3:0] HH_H,
  output [3:0] HH_L,
  output [3:0] MM_H,
  output [3:0] MM_L,
  output [3:0] SS_H,
  output [3:0] SS_L,
  output LED_R,
  output LED_G,
  output LED_B,
  output INErr
);

  wire and_1_out, and_2_out, and_3_out, and_4_out, and_5_out, and_6_out, and_7_out, and_8_out, and_9_out,
       and_10_out, and_11_out, and_12_out, and_13_out, and_18_out, and_19_out, and_20_out, and_21_out,
       and_23_out, cntr4u_4_q0, cntr4u_4_q1, cntr4u_4_q2, cntr4u_4_q3, LED_EN, not_1_out, not_2_out,
       or_1_out, or_2_out, or_3_out, or_4_out, or_5_out, or_6_out, or_7_out, or_8_out, or_10_out, START,
       STOP, xor_1_out, xor_2_out, xor_3_out;

  not not_1 (not_1_out, INErr);
  and and_1 (and_1_out, LD, not_1_out);
  and and_2 (and_2_out, HH1[0], HH1[1]);
  or or_1 (or_1_out, HH0[2], HH0[3]);
  or or_2 (or_2_out, HH0[1], HH0[2]);
  and and_3 (and_3_out, MM1[1], MM1[2]);
  or or_3 (or_3_out, MM0[1], MM0[2]);
  and and_4 (and_4_out, SS1[1], SS1[2]);
  or or_4 (or_4_out, SS0[1], SS0[2]);
  and and_5 (and_5_out, LED_EN, and_18_out);
  and and_6 (and_6_out, and_21_out, and_19_out);
  or or_5 (or_5_out, and_2_out, HH1[2], HH1[3]);
  and and_7 (and_7_out, HH1[1], or_1_out);
  and and_8 (and_8_out, or_2_out, HH0[3]);
  or or_6 (or_6_out, and_3_out, MM1[3]);
  and and_9 (and_9_out, or_3_out, MM0[3]);
  or or_7 (or_7_out, and_4_out, SS1[3]);
  and and_10 (and_10_out, or_4_out, SS0[3]);
  Hex_Digit_Display hex_digit_display_1 (.value(HH_H));  // open: dp
  CNTR4U cntr4u_1 (
    .CLK(CLK), .LD(and_1_out), .CLR(and_23_out), .Q0(HH_H[0]), .Q1(HH_H[1]), .D0(HH1[0]), .D1(HH1[1]),
    .D2(HH1[2]), .Q2(HH_H[2]), .Q3(HH_H[3]), .D3(HH1[3]), .ENP(and_5_out), .ENT(1'b1));  // open: RCO
  CNTR4U cntr4u_2 (
    .CLK(CLK), .LD(and_1_out), .CLR(LED_EN), .Q0(MM_H[0]), .Q1(MM_H[1]), .D0(MM1[0]), .D1(MM1[1]),
    .D2(MM1[2]), .Q2(MM_H[2]), .Q3(MM_H[3]), .D3(MM1[3]), .ENP(and_6_out), .ENT(1'b1));  // open: RCO
  CNTR4U cntr4u_3 (
    .CLK(CLK), .LD(and_1_out), .CLR(and_21_out), .Q0(SS_H[0]), .Q1(SS_H[1]), .D0(SS1[0]), .D1(SS1[1]),
    .D2(SS1[2]), .Q2(SS_H[2]), .Q3(SS_H[3]), .D3(SS1[3]), .ENP(and_20_out), .ENT(1'b1));  // open: RCO
  not not_2 (not_2_out, LED_EN);
  Hex_Digit_Display hex_digit_display_2 (.value(HH_L), .dp(1'b1));
  Hex_Digit_Display hex_digit_display_3 (.value(MM_H));  // open: dp
  CNTR4U cntr4u_4 (
    .CLK(CLK), .LD(LED_EN), .CLR(and_11_out), .Q0(cntr4u_4_q0), .Q1(cntr4u_4_q1), .D0(1'b1), .D1(1'b0),
    .D2(1'b0), .Q2(cntr4u_4_q2), .Q3(cntr4u_4_q3), .D3(1'b0), .ENP(START), .ENT(1'b1));  // open: RCO
  Hex_Digit_Display hex_digit_display_4 (.value(SS_H));  // open: dp
  Hex_Digit_Display hex_digit_display_5 (.value(MM_L), .dp(1'b1));
  or or_8 (or_8_out, or_5_out, and_7_out, and_8_out, or_6_out, and_9_out, or_7_out, and_10_out);
  or or_9 (START, cntr4u_4_q0, cntr4u_4_q1, cntr4u_4_q2, cntr4u_4_q3);
  and and_11 (and_11_out, cntr4u_4_q1, cntr4u_4_q3);
  xor xor_1 (xor_1_out, cntr4u_4_q0, cntr4u_4_q1);
  xor xor_2 (xor_2_out, cntr4u_4_q1, cntr4u_4_q2);
  xor xor_3 (xor_3_out, cntr4u_4_q2, 1'b0);
  Hex_Digit_Display hex_digit_display_6 (.value(SS_L), .dp(1'b1));
  or or_10 (or_10_out, and_23_out, and_12_out);
  and and_12 (and_12_out, and_18_out, LED_EN);
  and and_13 (and_13_out, and_19_out, and_21_out);
  and and_14 (INErr, LD, or_8_out);
  not not_3 (STOP, START);
  and and_15 (LED_R, xor_1_out, not_2_out);
  and and_16 (LED_G, xor_2_out, not_2_out);
  and and_17 (LED_B, xor_3_out, not_2_out);
  CNTR4U cntr4u_5 (
    .CLK(CLK), .LD(and_1_out), .CLR(or_10_out), .Q0(HH_L[0]), .Q1(HH_L[1]), .D0(HH0[0]), .D1(HH0[1]),
    .D2(HH0[2]), .Q2(HH_L[2]), .Q3(HH_L[3]), .D3(HH0[3]), .ENP(LED_EN), .ENT(1'b1));  // open: RCO
  CNTR4U cntr4u_6 (
    .CLK(CLK), .LD(and_1_out), .CLR(and_13_out), .Q0(MM_L[0]), .Q1(MM_L[1]), .D0(MM0[0]), .D1(MM0[1]),
    .D2(MM0[2]), .Q2(MM_L[2]), .Q3(MM_L[3]), .D3(MM0[3]), .ENP(and_21_out), .ENT(1'b1));  // open: RCO
  CNTR4U cntr4u_7 (
    .CLK(CLK), .LD(and_1_out), .CLR(and_20_out), .Q0(SS_L[0]), .Q1(SS_L[1]), .D0(SS0[0]), .D1(SS0[1]),
    .D2(SS0[2]), .Q2(SS_L[2]), .Q3(SS_L[3]), .D3(SS0[3]), .ENP(1'b1), .ENT(1'b1));  // open: RCO
  and and_18 (and_18_out, HH_L[0], HH_L[3]);
  and and_19 (and_19_out, MM_L[0], MM_L[3]);
  and and_20 (and_20_out, SS_L[0], SS_L[3]);
  // RGBLed RGBLED: pin names not known; wires that end beside it: LED_R, LED_G, LED_B
  and and_21 (and_21_out, and_20_out, SS_H[0], SS_H[2]);
  and and_22 (LED_EN, and_19_out, MM_H[0], MM_H[2], and_21_out);
  and and_23 (and_23_out, HH_L[0], HH_L[1], HH_H[1], LED_EN);

  // Other names for the same wires on the sheet: H0[3:0] = HH_L; H1[3:0] = HH_H; M0[3:0] = MM_L; M1[3:0] = MM_H;
  //   S0[3:0] = SS_L; S1[3:0] = SS_H

  // Notes on the sheet:
  //   设置初始时间BCD码
  //   输入信号
  //   请勿修改引脚名称、电路名称及电路封装外观
  //   数字时钟
  //   提示：使用4位二进制加法计数器子电路、比较器和独立逻辑门组件实现数字时钟。
  //   在载入有效时，检测设置数据错误
  //   生成三色LED显示信号，持续10个时钟周期
endmodule
