// Logisim project lab4.4.circ as structural Verilog: 1 circuit, main circuit main
// 移位器
module main (
  input  [4:0] shamt,
  input  L_R,
  input  A_L,
  input  [31:0] DataIn,
  output [31:0] DataOut
);

  wire and_3_out, and_5_out, and_7_out, and_9_out;
  wire [0:0] and_2_out;
  wire [1:0] and_4_out, bit_extender_1_out, bit_extender_2_out;
  wire [3:0] and_6_out, bit_extender_3_out, bit_extender_4_out;
  wire [7:0] and_8_out, bit_extender_5_out, bit_extender_6_out;
  wire [15:0] and_10_out, bit_extender_7_out, bit_extender_8_out;
  wire [31:0] multiplexer_1_out, multiplexer_2_out, multiplexer_3_out, multiplexer_4_out;
  wire [31:31] and_1_out;

  and and_1 (and_1_out[31], A_L, DataIn[31]);
  and and_2 (and_2_out[0], A_L, DataIn[31]);
  Multiplexer #(.select(2), .width(32), .enable("false")) multiplexer_1 (
    .in0(DataIn), .in1(DataIn), .in2({and_1_out[31], DataIn[31:1]}), .in3({DataIn[30:0], and_2_out[0]}),
    .out(multiplexer_1_out), .sel({shamt[0], L_R}));
  and and_3 (and_3_out, A_L, multiplexer_1_out[31]);
  assign bit_extender_1_out = {{1{A_L}}, A_L};  // Bit_Extender bit_extender_1
  assign bit_extender_2_out = {{1{and_3_out}}, and_3_out};  // Bit_Extender bit_extender_2
  assign and_4_out = bit_extender_1_out & multiplexer_1_out[31:30];  // AND_Gate and_4, 2 bits wide
  Multiplexer #(.select(2), .width(32), .enable("false")) multiplexer_2 (
    .in0(multiplexer_1_out), .in1(multiplexer_1_out), .in2({bit_extender_2_out, multiplexer_1_out[31:2]}),
    .in3({multiplexer_1_out[29:0], and_4_out}), .out(multiplexer_2_out), .sel({shamt[1], L_R}));
  and and_5 (and_5_out, A_L, multiplexer_2_out[31]);
  assign bit_extender_3_out = {{3{A_L}}, A_L};  // Bit_Extender bit_extender_3
  assign bit_extender_4_out = {{3{and_5_out}}, and_5_out};  // Bit_Extender bit_extender_4
  assign and_6_out = bit_extender_3_out & multiplexer_2_out[31:28];  // AND_Gate and_6, 4 bits wide
  Multiplexer #(.select(2), .width(32), .enable("false")) multiplexer_3 (
    .in0(multiplexer_2_out), .in1(multiplexer_2_out), .in2({bit_extender_4_out, multiplexer_2_out[31:4]}),
    .in3({multiplexer_2_out[27:0], and_6_out}), .out(multiplexer_3_out), .sel({shamt[2], L_R}));
  and and_7 (and_7_out, A_L, multiplexer_3_out[31]);
  assign bit_extender_5_out = {{7{A_L}}, A_L};  // Bit_Extender bit_extender_5
  assign bit_extender_6_out = {{7{and_7_out}}, and_7_out};  // Bit_Extender bit_extender_6
  assign and_8_out = bit_extender_5_out & multiplexer_3_out[31:24];  // AND_Gate and_8, 8 bits wide
  Multiplexer #(.select(2), .width(32), .enable("false")) multiplexer_4 (
    .in0(multiplexer_3_out), .in1(multiplexer_3_out), .in2({bit_extender_6_out, multiplexer_3_out[31:8]}),
    .in3({multiplexer_3_out[23:0], and_8_out}), .out(multiplexer_4_out), .sel({shamt[3], L_R}));
  assign bit_extender_7_out = {{15{and_9_out}}, and_9_out};  // Bit_Extender bit_extender_7
  and and_9 (and_9_out, A_L, multiplexer_4_out[31]);
  assign bit_extender_8_out = {{15{A_L}}, A_L};  // Bit_Extender bit_extender_8
  assign and_10_out = bit_extender_8_out & multiplexer_4_out[31:16];  // AND_Gate and_10, 16 bits wide
  Multiplexer #(.select(2), .width(32), .enable("false")) multiplexer_5 (
    .in0(multiplexer_4_out), .in1(multiplexer_4_out), .in2({bit_extender_7_out, multiplexer_4_out[31:16]}),
    .in3({multiplexer_4_out[15:0], and_10_out}), .out(DataOut), .sel({shamt[4], L_R}));

  // Other names for the same wires on the sheet: Din[31:0] = DataIn; Left_Right = L_R; Arth_Logic = A_L;
  //   Dout[31:0] = DataOut

  // Notes on the sheet:
  //   L/R,A/L: 00逻辑右移，01算术右移，10逻辑左移，11：循环左移
  //   输入引脚
  //   请勿修改引脚名称、电路名称及电路封装外观
  //   提示：使用多路选择器、逻辑门实现32位桶形移位器，禁止直接使用移位器组件。
  //   输出引脚
endmodule
