// Logisim project lab4.5.circ as structural Verilog: 8 circuits, main circuit ALU
module ALU (
  input  [3:0] ALUctr,
  input  [31:0] A,
  input  [31:0] B,
  output Zero,
  output [31:0] S
);

  wire adder32_1_cf, adder32_1_of, adder32_1_sf, aluctrl_1_alctr, aluctrl_1_lrctr, aluctrl_1_sigctr,
       aluctrl_1_subctr, multiplexer_1_out, xor_3_out;
  wire [2:0] aluctrl_1_opctr;
  wire [31:0] adder32_1_s, and_1_out, bit_extender_1_out, bit_extender_2_out, or_1_out, shifter32_1_dataout,
       xor_1_out, xor_2_out;

  assign bit_extender_1_out = {{31{aluctrl_1_subctr}}, aluctrl_1_subctr};  // Bit_Extender bit_extender_1
  assign xor_1_out = B ^ bit_extender_1_out;  // XOR_Gate xor_1, 32 bits wide
  assign and_1_out = A & B;  // AND_Gate and_1, 32 bits wide
  assign or_1_out = A | B;  // OR_Gate or_1, 32 bits wide
  assign xor_2_out = A ^ B;  // XOR_Gate xor_2, 32 bits wide
  Shifter32 shifter32_1 (
    .DataIn(A), .shamt(B[4:0]), .L_R(aluctrl_1_lrctr), .A_L(aluctrl_1_alctr), .DataOut(shifter32_1_dataout));
  Adder32 adder32_1 (
    .CF(adder32_1_cf), .OF(adder32_1_of), .SF(adder32_1_sf), .ZF(Zero), .X(A), .Y(xor_1_out),
    .Cin(aluctrl_1_subctr), .S(adder32_1_s));  // open: Cout
  xor xor_3 (xor_3_out, adder32_1_of, adder32_1_sf);
  Multiplexer #(.enable("false")) multiplexer_1 (
    .in0(adder32_1_cf), .in1(xor_3_out), .out(multiplexer_1_out), .sel(aluctrl_1_sigctr));
  Multiplexer #(.select(3), .width(32), .enable("false")) multiplexer_2 (
    .in0(adder32_1_s), .in1(and_1_out), .in2(or_1_out), .in3(xor_2_out), .in4(shifter32_1_dataout), .in5(B),
    .in6(bit_extender_2_out), .out(S), .sel(aluctrl_1_opctr));  // open: in7
  ALUctrl aluctrl_1 (
    .SUBctr(aluctrl_1_subctr), .LRctr(aluctrl_1_lrctr), .SIGctr(aluctrl_1_sigctr), .ALctr(aluctrl_1_alctr),
    .OPctr(aluctrl_1_opctr), .ALUctr(ALUctr));
  assign bit_extender_2_out = {{31{1'b0}}, multiplexer_1_out};  // Bit_Extender bit_extender_2
  // Probe on A
  // Probe on B
  // Probe on S

  // Other names for the same wires on the sheet: Result[31:0] = S

  // Notes on the sheet:
  //   ALUctr: pull=down
  //   A: pull=down
  //   B: pull=down
  //   输入引脚
  //   请勿修改引脚名称、电路名称及电路封装外观
  //   提示：使用32位并行加法器子电路、桶形移位器、ALU控制子电路实现32位ALU
  //   功能说明:32位ALU，输入32位操作数A、B，4位控制信号ALUctr，输出32位结果Reseult和1位Zero标志位
  //   输出引脚
  //   操作数和结果
endmodule

module ALUctrl (
  input  [3:0] ALUctr,
  output SUBctr,
  output LRctr,
  output SIGctr,
  output ALctr,
  output [2:0] OPctr
);

  wire and_1_out, and_2_out, and_3_out, and_7_out, and_8_out, and_9_out, and_10_out, and_11_out, and_12_out,
       and_13_out, and_14_out, and_15_out, and_16_out, and_17_out, and_18_out, and_19_out, not_1_out,
       not_2_out, not_3_out, not_4_out;

  not not_1 (not_1_out, ALUctr[1]);
  not not_2 (not_2_out, ALUctr[2]);
  not not_3 (not_3_out, ALUctr[3]);
  not not_4 (not_4_out, ALUctr[0]);
  and and_1 (and_1_out, not_4_out, ALUctr[1], not_2_out, not_3_out);
  or or_1 (SUBctr, and_1_out, and_2_out, and_3_out);
  and and_2 (and_2_out, ALUctr[0], ALUctr[1], not_2_out, not_3_out);
  and and_3 (and_3_out, not_4_out, not_1_out, not_2_out, ALUctr[3]);
  and and_4 (SIGctr, not_4_out, ALUctr[1], not_2_out, not_3_out);
  and and_5 (ALctr, ALUctr[0], not_1_out, ALUctr[2], ALUctr[3]);
  and and_6 (LRctr, ALUctr[0], not_1_out, not_2_out, not_3_out);
  and and_7 (and_7_out, not_4_out, not_1_out, ALUctr[2], not_3_out);
  or or_2 (OPctr[0], and_7_out, and_8_out, and_9_out);
  and and_8 (and_8_out, ALUctr[0], ALUctr[1], ALUctr[2], not_3_out);
  and and_9 (and_9_out, ALUctr[0], ALUctr[1], ALUctr[2], ALUctr[3]);
  and and_10 (and_10_out, not_4_out, ALUctr[1], not_2_out, not_3_out);
  and and_11 (and_11_out, ALUctr[0], ALUctr[1], not_2_out, not_3_out);
  or or_3 (OPctr[1], and_10_out, and_11_out, and_12_out, and_13_out);
  and and_12 (and_12_out, not_4_out, not_1_out, ALUctr[2], not_3_out);
  and and_13 (and_13_out, not_4_out, ALUctr[1], ALUctr[2], not_3_out);
  and and_14 (and_14_out, ALUctr[0], not_1_out, not_2_out, not_3_out);
  and and_15 (and_15_out, not_4_out, ALUctr[1], not_2_out, not_3_out);
  and and_16 (and_16_out, ALUctr[0], ALUctr[1], not_2_out, not_3_out);
  and and_17 (and_17_out, ALUctr[0], not_1_out, ALUctr[2], not_3_out);
  and and_18 (and_18_out, ALUctr[0], not_1_out, ALUctr[2], ALUctr[3]);
  and and_19 (and_19_out, ALUctr[0], ALUctr[1], ALUctr[2], ALUctr[3]);
  or or_4 (OPctr[2], and_14_out, and_15_out, and_16_out, and_17_out, and_18_out, and_19_out);

  // Notes on the sheet:
  //   输入引脚
  //   ALU操作控制信号生成部件
  //   输出引脚
endmodule

module Adder32 (
  input  Cin,
  input  [31:0] X,
  input  [31:0] Y,
  output CF,
  output Cout,
  output OF,
  output SF,
  output [31:0] S,
  output ZF
);

  wire adder16_2_c16, and_1_out, and_2_out, not_1_out, not_2_out, not_3_out;

  not not_1 (not_1_out, X[31]);
  not not_2 (not_2_out, Y[31]);
  not not_3 (not_3_out, S[31]);
  Adder16 adder16_1 (.X(X[31:16]), .Y(Y[31:16]), .C0(adder16_2_c16), .S(S[31:16]), .C16(Cout));  // open: Pg, Gg
  and and_1 (and_1_out, X[31], Y[31], not_3_out);
  and and_2 (and_2_out, not_1_out, not_2_out, S[31]);
  Adder16 adder16_2 (.X(X[15:0]), .Y(Y[15:0]), .C0(Cin), .S(S[15:0]), .C16(adder16_2_c16));  // open: Pg, Gg
  xor xor_1 (CF, Cin, Cout);
  or or_1 (OF, and_1_out, and_2_out);
  nor nor_1 (ZF, S[0], S[1], S[2], S[3], S[4], S[5], S[6], S[7], S[8], S[9], S[10], S[11], S[12], S[13], S[14], S[15], S[17], S[18], S[19], S[20], S[21], S[22], S[23], S[24], S[25], S[26], S[27], S[28], S[29], S[30], S[31], S[16]);
  // Probe on X
  // Probe on Y
  // Probe on S

  assign SF = S[31];

  // Notes on the sheet:
  //   Cin: pull=down
  //   Y: pull=down
  //   X: pull=down
  //   输入引脚区
  //   输出引脚区
  //   请勿修改引脚名称、电路名称及电路封装外观
  //   提示：使用16位并行加法器子电路实现32位快速加法器
  //   功能说明:32位Adder  S=X+Y，Cout为最高位进位位，Cin为进位输入， S为和，溢出OF、进位CF、零ZF、符号SF。
  //   +
  //   =
  //   无符号加法
endmodule

// 移位器
module Shifter32 (
  input  [4:0] shamt,
  input  L_R,
  input  A_L,
  input  [31:0] DataIn,
  output [31:0] DataOut
);

  wire and_3_out, and_5_out, and_7_out, and_9_out;
  wire [0:0] and_2_out;
  wire [1:0] and_4_out, bit_extender_1_out, bit_extender_2_out;
  wire [3:0] and_6_out, bit_extender_3_out, bit_extender_4_out;
  wire [7:0] and_8_out, bit_extender_5_out, bit_extender_6_out;
  wire [15:0] and_10_out, bit_extender_7_out, bit_extender_8_out;
  wire [31:0] multiplexer_1_out, multiplexer_2_out, multiplexer_3_out, multiplexer_4_out;
  wire [31:31] and_1_out;

  and and_1 (and_1_out[31], A_L, DataIn[31]);
  and and_2 (and_2_out[0], A_L, DataIn[31]);
  Multiplexer #(.select(2), .width(32), .enable("false")) multiplexer_1 (
    .in0(DataIn), .in1(DataIn), .in2({and_1_out[31], DataIn[31:1]}), .in3({DataIn[30:0], and_2_out[0]}),
    .out(multiplexer_1_out), .sel({shamt[0], L_R}));
  and and_3 (and_3_out, A_L, multiplexer_1_out[31]);
  assign bit_extender_1_out = {{1{A_L}}, A_L};  // Bit_Extender bit_extender_1
  Multiplexer #(.select(2), .width(32), .enable("false")) multiplexer_2 (
    .in0(multiplexer_1_out), .in1(multiplexer_1_out), .in2({bit_extender_2_out, multiplexer_1_out[31:2]}),
    .in3({multiplexer_1_out[29:0], and_4_out}), .out(multiplexer_2_out), .sel({shamt[1], L_R}));
  assign bit_extender_2_out = {{1{and_3_out}}, and_3_out};  // Bit_Extender bit_extender_2
  assign and_4_out = bit_extender_1_out & multiplexer_1_out[31:30];  // AND_Gate and_4, 2 bits wide
  and and_5 (and_5_out, A_L, multiplexer_2_out[31]);
  assign bit_extender_3_out = {{3{A_L}}, A_L};  // Bit_Extender bit_extender_3
  assign bit_extender_4_out = {{3{and_5_out}}, and_5_out};  // Bit_Extender bit_extender_4
  assign and_6_out = bit_extender_3_out & multiplexer_2_out[31:28];  // AND_Gate and_6, 4 bits wide
  Multiplexer #(.select(2), .width(32), .enable("false")) multiplexer_3 (
    .in0(multiplexer_2_out), .in1(multiplexer_2_out), .in2({bit_extender_4_out, multiplexer_2_out[31:4]}),
    .in3({multiplexer_2_out[27:0], and_6_out}), .out(multiplexer_3_out), .sel({shamt[2], L_R}));
  and and_7 (and_7_out, A_L, multiplexer_3_out[31]);
  assign bit_extender_5_out = {{7{A_L}}, A_L};  // Bit_Extender bit_extender_5
  assign bit_extender_6_out = {{7{and_7_out}}, and_7_out};  // Bit_Extender bit_extender_6
  assign and_8_out = bit_extender_5_out & multiplexer_3_out[31:24];  // AND_Gate and_8, 8 bits wide
  Multiplexer #(.select(2), .width(32), .enable("false")) multiplexer_4 (
    .in0(multiplexer_3_out), .in1(multiplexer_3_out), .in2({bit_extender_6_out, multiplexer_3_out[31:8]}),
    .in3({multiplexer_3_out[23:0], and_8_out}), .out(multiplexer_4_out), .sel({shamt[3], L_R}));
  and and_9 (and_9_out, A_L, multiplexer_4_out[31]);
  assign bit_extender_7_out = {{15{A_L}}, A_L};  // Bit_Extender bit_extender_7
  assign bit_extender_8_out = {{15{and_9_out}}, and_9_out};  // Bit_Extender bit_extender_8
  assign and_10_out = bit_extender_7_out & multiplexer_4_out[31:16];  // AND_Gate and_10, 16 bits wide
  Multiplexer #(.select(2), .width(32), .enable("false")) multiplexer_5 (
    .in0(multiplexer_4_out), .in1(multiplexer_4_out), .in2({bit_extender_8_out, multiplexer_4_out[31:16]}),
    .in3({multiplexer_4_out[15:0], and_10_out}), .out(DataOut), .sel({shamt[4], L_R}));

  // Other names for the same wires on the sheet: Din[31:0] = DataIn; Left_Right = L_R; Arth_Logic = A_L;
  //   Dout[31:0] = DataOut

  // Notes on the sheet:
  //   L/R,A/L: 00逻辑右移，01算术右移，10逻辑左移，11：循环左移
  //   输入引脚
  //   请勿修改引脚名称、电路名称及电路封装外观
  //   提示：使用多路选择器、逻辑门实现32位桶形移位器，禁止直接使用移位器组件。
  //   输出引脚
endmodule

module Adder16 (
  input  C0,
  input  [15:0] X,
  input  [15:0] Y,
  output C16,
  output Pg,
  output Gg,
  output [15:0] S
);

  wire cla4_1_gg, cla4_1_pg, cla4_2_gg, cla4_2_pg, cla4_3_gg, cla4_3_pg, cla4_4_gg, cla4_4_pg, clu4_1_c1,
       clu4_1_c2, clu4_1_c3;

  CLA4 cla4_1 (
    .X(X[15:12]), .F(S[15:12]), .Y(Y[15:12]), .Pg(cla4_1_pg), .Cin(clu4_1_c3), .Gg(cla4_1_gg));  // open: Cout
  CLA4 cla4_2 (.X(X[11:8]), .F(S[11:8]), .Y(Y[11:8]), .Pg(cla4_2_pg), .Cin(clu4_1_c2), .Gg(cla4_2_gg));  // open: Cout
  CLU4 clu4_1 (
    .P0(cla4_4_pg), .P1(cla4_3_pg), .P2(cla4_2_pg), .P3(cla4_1_pg), .C1(clu4_1_c1), .C3(clu4_1_c3),
    .G0(cla4_4_gg), .G1(cla4_3_gg), .G2(cla4_2_gg), .G3(cla4_1_gg), .C2(clu4_1_c2), .C4(C16), .C0(C0),
    .Pg(Pg), .Gg(Gg));
  CLA4 cla4_3 (.X(X[7:4]), .F(S[7:4]), .Y(Y[7:4]), .Pg(cla4_3_pg), .Cin(clu4_1_c1), .Gg(cla4_3_gg));  // open: Cout
  CLA4 cla4_4 (.X(X[3:0]), .F(S[3:0]), .Y(Y[3:0]), .Pg(cla4_4_pg), .Cin(C0), .Gg(cla4_4_gg));  // open: Cout
  // Probe on X
  // Probe on Y
  // Probe on S

  // Notes on the sheet:
  //   X: pull=down
  //   Y: pull=down
  //   C0: pull=down
  //   输入引脚区
  //   请勿修改引脚名称、电路名称及电路封装外观
  //   提示：使用4位先行进位加法器和CLU子电路实现16位并行加法器
  //   功能说明:16位Adder  S=X+Y，C16为最高位进位位，C0为进位输入， Pg、Gg为成组进位生成传递函数
  //   输出引脚区
  //   +
  //   =
  //   无符号加法
endmodule

module CLA4 (
  input  [3:0] X,
  input  [3:0] Y,
  input  Cin,
  output [3:0] F,
  output Cout,
  output Pg,
  output Gg
);

  wire clu4_1_c1, clu4_1_c2, clu4_1_c3, fa_1_g, fa_1_p, fa_2_g, fa_2_p, fa_3_g, fa_3_p, fa_4_g, fa_4_p;

  Hex_Digit_Display hex_digit_display_1 (.value(X));  // open: dp
  FA fa_1 (.A(X[3]), .F(F[3]), .B(Y[3]), .P(fa_1_p), .Cin(clu4_1_c3), .G(fa_1_g));
  Hex_Digit_Display hex_digit_display_2 (.value(Y));  // open: dp
  FA fa_2 (.A(X[2]), .F(F[2]), .B(Y[2]), .P(fa_2_p), .Cin(clu4_1_c2), .G(fa_2_g));
  FA fa_3 (.A(X[1]), .F(F[1]), .B(Y[1]), .P(fa_3_p), .Cin(clu4_1_c1), .G(fa_3_g));
  Hex_Digit_Display hex_digit_display_3 (.value(F));  // open: dp
  CLU4 clu4_1 (
    .P0(fa_4_p), .P1(fa_3_p), .P2(fa_2_p), .P3(fa_1_p), .C1(clu4_1_c1), .C3(clu4_1_c3), .G0(fa_4_g),
    .G1(fa_3_g), .G2(fa_2_g), .G3(fa_1_g), .C2(clu4_1_c2), .C4(Cout), .C0(Cin), .Pg(Pg), .Gg(Gg));
  FA fa_4 (.A(X[0]), .F(F[0]), .B(Y[0]), .P(fa_4_p), .Cin(Cin), .G(fa_4_g));

  // Other names for the same wires on the sheet: Z[3:0] = F

  // Notes on the sheet:
  //   +
  //   =
  //   输出
  //   输入
  //   请勿修改引脚名称、电路名称及电路封装外观
  //   提示：使用全加器和CLU子电路实现四位先行进位加法器CLA4
endmodule

module CLU4 (
  input  P0,
  input  P1,
  input  P2,
  input  P3,
  input  G0,
  input  G1,
  input  G2,
  input  G3,
  input  C0,
  output C1,
  output C3,
  output C2,
  output C4,
  output Pg,
  output Gg
);

  wire and_1_out, and_2_out, and_4_out, and_5_out, and_6_out, and_7_out, and_8_out, and_9_out, and_10_out,
       and_11_out, and_12_out, and_13_out, and_14_out;

  or or_1 (C4, G3, and_2_out, and_1_out, and_4_out, and_5_out);
  and and_1 (and_1_out, P3, P2, G1);
  and and_2 (and_2_out, P3, G2);
  and and_3 (Pg, P3, P2, P1, P0);
  and and_4 (and_4_out, P3, P2, P1, G0);
  and and_5 (and_5_out, P3, P2, P1, P0, C0);
  and and_6 (and_6_out, P3, G2);
  and and_7 (and_7_out, P3, P2, G1);
  and and_8 (and_8_out, P3, P2, P1, G0);
  or or_2 (C3, G2, and_10_out, and_9_out, and_11_out);
  and and_9 (and_9_out, P2, P1, G0);
  and and_10 (and_10_out, P2, G1);
  and and_11 (and_11_out, P2, P1, P0, C0);
  or or_3 (Gg, G3, and_6_out, and_7_out, and_8_out);
  and and_12 (and_12_out, P1, G0);
  or or_4 (C2, G1, and_12_out, and_13_out);
  and and_13 (and_13_out, P1, P0, C0);
  or or_5 (C1, G0, and_14_out);
  and and_14 (and_14_out, P0, C0);

  // Notes on the sheet:
  //   输入引脚
  //   请勿修改引脚名称、电路名称及电路封装外观
  //   提示：使用逻辑门电路实现4位四位先行进位部件CLU，Pg、Gg为成组进位生成传递函数
  //   输出引脚
endmodule

module FA (
  input  A,
  input  B,
  input  Cin,
  output F,
  output P,
  output G
);

  ExactlyOne xor_1 (.out(F), .in0(A), .in1(B), .in2(Cin));
  or or_1 (P, A, B);
  and and_1 (G, A, B);

  // Notes on the sheet:
  //   输入引脚
  //   请勿修改引脚名称、电路名称及电路封装外观
  //   全加器
  //   输出引脚
endmodule
