// Logisim project lab5.2.circ as structural Verilog: 1 circuit, main circuit DataRam
// DataRAM
module DataRam (
  input  CLK,
  input  CLR,
  input  WE,
  input  [2:0] MemOp,
  input  [17:0] Addr,
  input  [31:0] Din,
  output AlignErr,
  output [31:0] DataOut
);

  wire and_1_out, and_2_out, and_3_out, and_4_out, and_5_out, and_6_out, and_7_out, and_8_out, and_9_out,
       and_10_out, and_11_out, and_12_out, and_13_out, and_14_out, and_15_out, and_16_out, and_17_out,
       and_18_out, and_19_out, and_20_out, and_21_out, and_22_out, and_23_out, ld, not_1_out, not_2_out,
       not_3_out, not_4_out, not_5_out, or_5_out, str;
  wire [3:0] SEL;
  wire [7:0] D0, D1, D2, D3, multiplexer_1_out, multiplexer_2_out, multiplexer_3_out, multiplexer_4_out,
       multiplexer_5_out;
  wire [15:0] multiplexer_6_out;
  wire [31:0] bit_extender_1_out, bit_extender_2_out, bit_extender_3_out, bit_extender_4_out;

  not not_1 (not_1_out, MemOp[2]);
  not not_2 (not_2_out, MemOp[1]);
  not not_3 (not_3_out, Addr[1]);
  not not_4 (not_4_out, MemOp[0]);
  not not_5 (not_5_out, Addr[0]);
  and and_1 (and_1_out, not_5_out, not_3_out, not_4_out, not_2_out, not_1_out);
  and and_2 (and_2_out, Addr[0], Addr[1], MemOp[0], not_2_out);
  and and_3 (and_3_out, not_5_out, Addr[1], not_4_out, MemOp[1]);
  and and_4 (and_4_out, not_5_out, not_3_out, not_4_out, not_2_out, not_1_out);
  and and_5 (and_5_out, not_5_out, Addr[1], MemOp[0], not_2_out);
  and and_6 (and_6_out, not_5_out, Addr[1], not_4_out, MemOp[1]);
  and and_7 (and_7_out, not_5_out, not_3_out, not_4_out, not_2_out, not_1_out);
  and and_8 (and_8_out, Addr[0], not_3_out, MemOp[0], not_2_out);
  and and_9 (and_9_out, not_5_out, not_3_out, not_4_out, MemOp[1]);
  and and_10 (and_10_out, not_5_out, not_3_out, not_4_out, not_2_out, not_1_out);
  and and_11 (and_11_out, not_5_out, not_3_out, MemOp[0], not_2_out);
  and and_12 (and_12_out, not_5_out, not_3_out, not_4_out, MemOp[1]);
  and and_13 (and_13_out, not_5_out, not_3_out, not_4_out, not_2_out, not_1_out);
  and and_14 (and_14_out, MemOp[0], not_2_out);
  and and_15 (and_15_out, not_5_out, not_4_out, MemOp[1]);
  and and_16 (and_16_out, not_4_out, not_2_out, not_1_out);
  and and_17 (and_17_out, MemOp[0], not_2_out, MemOp[2]);
  and and_18 (and_18_out, not_4_out, MemOp[1], MemOp[2]);
  and and_19 (and_19_out, not_4_out, not_2_out, not_1_out);
  and and_20 (and_20_out, MemOp[0], not_2_out, not_1_out);
  and and_21 (and_21_out, not_4_out, MemOp[1], not_1_out);
  and and_22 (and_22_out, MemOp[0], not_2_out, MemOp[2]);
  and and_23 (and_23_out, not_4_out, MemOp[1], MemOp[2]);
  or or_1 (SEL[3], and_1_out, and_2_out, and_3_out);
  or or_2 (SEL[2], and_4_out, and_5_out, and_6_out);
  or or_3 (SEL[1], and_7_out, and_8_out, and_9_out);
  or or_4 (SEL[0], and_10_out, and_11_out, and_12_out);
  nor nor_1 (AlignErr, and_13_out, and_14_out, and_15_out);
  or or_5 (or_5_out, and_16_out, and_17_out, and_18_out);
  and and_24 (str, or_5_out, WE);
  or or_6 (ld, and_19_out, and_20_out, and_21_out, and_22_out, and_23_out);
  Multiplexer #(.select(4), .width(8), .enable("false")) multiplexer_1 (
    .in8(Din[7:0]), .in12(Din[15:8]), .in15(Din[31:24]), .out(multiplexer_1_out), .sel(SEL));  // open: in0, in1, in2, in3, in4, in5, in6, in7, in9, in10, in11, in13, in14
  Multiplexer #(.select(4), .width(8), .enable("false")) multiplexer_2 (
    .in2(Din[7:0]), .in3(Din[15:8]), .in15(Din[15:8]), .out(multiplexer_2_out), .sel(SEL));  // open: in0, in1, in4, in5, in6, in7, in8, in9, in10, in11, in12, in13, in14
  Multiplexer #(.select(4), .width(8), .enable("false")) multiplexer_3 (
    .in4(Din[7:0]), .in12(Din[7:0]), .in15(Din[23:16]), .out(multiplexer_3_out), .sel(SEL));  // open: in0, in1, in2, in3, in5, in6, in7, in8, in9, in10, in11, in13, in14
  Multiplexer #(.select(4), .width(8), .enable("false")) multiplexer_4 (
    .in1(Din[7:0]), .in3(Din[7:0]), .in15(Din[7:0]), .out(multiplexer_4_out), .sel(SEL));  // open: in0, in2, in4, in5, in6, in7, in8, in9, in10, in11, in12, in13, in14
  RAM #(.addrWidth(16), .bus("separate"), .Select("high")) ram_1 (
    .addr(Addr[17:2]), .din(multiplexer_1_out), .data(D3), .str(str), .sel(SEL[3]), .clk(CLK), .ld(ld),
    .clr(CLR));
  RAM #(.addrWidth(16), .bus("separate"), .Select("high")) ram_2 (
    .addr(Addr[17:2]), .din(multiplexer_3_out), .data(D2), .str(str), .sel(SEL[2]), .clk(CLK), .ld(ld),
    .clr(CLR));
  RAM #(.addrWidth(16), .bus("separate"), .Select("high")) ram_3 (
    .addr(Addr[17:2]), .din(multiplexer_2_out), .data(D1), .str(str), .sel(SEL[1]), .clk(CLK), .ld(ld),
    .clr(CLR));
  RAM #(.addrWidth(16), .bus("separate"), .Select("high")) ram_4 (
    .addr(Addr[17:2]), .din(multiplexer_4_out), .data(D0), .str(str), .sel(SEL[0]), .clk(CLK), .ld(ld),
    .clr(CLR));
  Multiplexer #(.select(2), .width(8), .enable("false")) multiplexer_5 (
    .in0(D0), .in1(D1), .in2(D2), .in3(D3), .out(multiplexer_5_out), .sel(Addr[1:0]));
  Multiplexer #(.width(16), .enable("false")) multiplexer_6 (
    .in0({D1, D0}), .in1({D3, D2}), .out(multiplexer_6_out), .sel(Addr[1]));
  assign bit_extender_1_out = {{24{1'b0}}, multiplexer_5_out};  // Bit_Extender bit_extender_1
  assign bit_extender_2_out = {{24{multiplexer_5_out[7]}}, multiplexer_5_out};  // Bit_Extender bit_extender_2
  assign bit_extender_3_out = {{16{1'b0}}, multiplexer_6_out};  // Bit_Extender bit_extender_3
  assign bit_extender_4_out = {{16{multiplexer_6_out[15]}}, multiplexer_6_out};  // Bit_Extender bit_extender_4
  Multiplexer #(.select(3), .width(32), .enable("false")) multiplexer_7 (
    .in0({D3, D2, D1, D0}), .in1(bit_extender_1_out), .in2(bit_extender_3_out), .in5(bit_extender_2_out),
    .in6(bit_extender_4_out), .out(DataOut), .sel(MemOp));  // open: in3, in4, in7

  // Other names for the same wires on the sheet: addr0_1[1:0] = Addr[1:0]; Dout[31:0] = DataOut

  // Notes on the sheet:
  //   输入引脚
  //   请勿修改引脚名称、电路名称及电路封装外观
  //   为了后续实验中的引用，不要修改MemOp的编码定义、引脚名称和在布局中的位置。
  //   32位数据存储器，按字节分4片存储，可按照字节、半字和字进行存储；读取字节或半字时，支持0扩展和符号位扩展。
  //   输出引脚
endmodule
