// Logisim project lab6.1.circ as structural Verilog: 1 circuit, main circuit 控制器
module \控制器  (
  input  [6:0] opcode,
  input  [2:0] funct3,
  input  [6:0] funct7,
  output [2:0] ExtOp,
  output RegWr,
  output [2:0] BandJ,
  output ALUASrc,
  output [1:0] ALUBSrc,
  output [3:0] ALUctr,
  output MemtoReg,
  output [2:0] MemOp,
  output MemWr
);

  wire and_out, andi_out, auipc_out, bge_u_out, blt_ge_u_out, blt_u_out, bne_out, comparator_1_eq,
       I_type_ALU_out, I_type_jalr_out, lb_out, lbu_out, lh_out, lhu_out, lui_out, not_1_out, not_2_out,
       not_3_out, not_4_out, not_5_out, not_6_out, not_7_out, not_8_out, not_9_out, not_10_out, not_11_out,
       not_12_out, not_13_out, not_14_out, or_out, ori_out, R_type_out, sb_out, sh_out, sll_out, slli_out,
       slt_out, slti_out, sltiu_out, sltu_out, sra_out, srai_out, srl_out, srli_out, sub_out, U_type_out,
       xor_out, xori_out;

  not not_1 (not_1_out, funct7[5]);
  Comparator #(.width(6)) comparator_1 (
    .a({6{1'b0}}), .b({funct7[6], funct7[4:0]}), .eq(comparator_1_eq));  // open: gt, lt
  not not_2 (not_2_out, opcode[0]);
  not not_3 (not_3_out, opcode[1]);
  not not_4 (not_4_out, opcode[2]);
  not not_5 (not_5_out, opcode[3]);
  not not_6 (not_6_out, opcode[4]);
  not not_7 (not_7_out, opcode[5]);
  not not_8 (not_8_out, opcode[6]);
  and R_type (R_type_out, not_8_out, opcode[5], opcode[4], not_5_out, not_4_out, opcode[1], opcode[0]);
  not not_9 (not_9_out, funct3[0]);
  not not_10 (not_10_out, funct3[1]);
  not not_11 (not_11_out, funct3[2]);
  not not_12 (not_12_out, funct3[2]);
  not not_13 (not_13_out, funct3[1]);
  not not_14 (not_14_out, funct3[0]);
  and I_type_ALU (I_type_ALU_out, not_8_out, not_7_out, opcode[4], not_5_out, not_4_out, opcode[1], opcode[0]);
  and \and  (and_out, funct3[2], funct3[1], funct3[0], not_1_out, comparator_1_eq, R_type_out);
  and sra (sra_out, funct3[2], not_13_out, funct3[0], funct7[5], comparator_1_eq, R_type_out);
  and sltu (sltu_out, not_12_out, funct3[1], funct3[0], not_1_out, comparator_1_eq, R_type_out);
  and srl (srl_out, funct3[2], not_13_out, funct3[0], not_1_out, comparator_1_eq, R_type_out);
  and sll (sll_out, not_12_out, not_13_out, funct3[0], not_1_out, comparator_1_eq, R_type_out);
  and slt (slt_out, not_12_out, funct3[1], not_14_out, not_1_out, comparator_1_eq, R_type_out);
  and \or  (or_out, funct3[2], funct3[1], not_14_out, not_1_out, comparator_1_eq, R_type_out);
  and \xor  (xor_out, funct3[2], not_13_out, not_14_out, not_1_out, comparator_1_eq, R_type_out);
  and sub (sub_out, not_12_out, not_13_out, not_14_out, funct7[5], comparator_1_eq, R_type_out);
  and I_type_load (MemtoReg, not_8_out, not_7_out, not_6_out, not_5_out, not_4_out, opcode[1], opcode[0]);
  and andi (andi_out, funct3[2], funct3[1], funct3[0], I_type_ALU_out);
  and srai (srai_out, funct3[2], not_13_out, funct3[0], funct7[5], comparator_1_eq, I_type_ALU_out);
  and sltiu (sltiu_out, not_12_out, funct3[1], funct3[0], I_type_ALU_out);
  and srli (srli_out, funct3[2], not_13_out, funct3[0], not_1_out, comparator_1_eq, I_type_ALU_out);
  and slli (slli_out, not_12_out, not_13_out, funct3[0], not_1_out, comparator_1_eq, I_type_ALU_out);
  and slti (slti_out, not_12_out, funct3[1], not_14_out, I_type_ALU_out);
  and ori (ori_out, funct3[2], funct3[1], not_14_out, I_type_ALU_out);
  and xori (xori_out, funct3[2], not_13_out, not_14_out, I_type_ALU_out);
  and S_type (MemWr, not_8_out, opcode[5], not_6_out, not_5_out, not_4_out, opcode[1], opcode[0]);
  and lb (lb_out, not_12_out, not_13_out, not_14_out, MemtoReg);
  and lbu (lbu_out, funct3[2], not_13_out, not_14_out, MemtoReg);
  and lh (lh_out, not_12_out, not_13_out, funct3[0], MemtoReg);
  and lhu (lhu_out, funct3[2], not_13_out, funct3[0], MemtoReg);
  and B_type (BandJ[2], opcode[6], opcode[5], not_6_out, not_5_out, not_4_out, opcode[1], opcode[0]);
  and sb (sb_out, not_12_out, not_13_out, not_14_out, MemWr);
  and sh (sh_out, not_12_out, not_13_out, funct3[0], MemWr);
  and J_type (ExtOp[2], opcode[6], opcode[5], not_6_out, opcode[3], opcode[2], opcode[1], opcode[0]);
  and bne (bne_out, not_12_out, not_13_out, funct3[0], BandJ[2]);
  and bge_u (bge_u_out, funct3[2], funct3[0], BandJ[2]);
  and blt_u (blt_u_out, funct3[2], not_14_out, BandJ[2]);
  and blt_ge_u (blt_ge_u_out, funct3[2], funct3[1], BandJ[2]);
  and I_type_jalr (I_type_jalr_out, opcode[6], opcode[5], not_6_out, not_5_out, opcode[2], opcode[1], opcode[0], not_11_out, not_10_out, not_9_out);
  and U_type (U_type_out, not_8_out, 1'b1, opcode[4], not_5_out, opcode[2], opcode[1], opcode[0]);
  or or_2 (RegWr, R_type_out, I_type_ALU_out, MemtoReg, ExtOp[2], I_type_jalr_out, U_type_out);
  or or_3 (BandJ[0], ExtOp[2], bne_out, bge_u_out);
  or or_4 (BandJ[1], I_type_jalr_out, bge_u_out, blt_u_out);
  and auipc (auipc_out, not_7_out, U_type_out);
  or or_5 (ALUASrc, auipc_out, ExtOp[2], I_type_jalr_out);
  or or_6 (ALUBSrc[0], ExtOp[2], I_type_jalr_out);
  or or_7 (ALUBSrc[1], U_type_out, I_type_ALU_out, MemtoReg, MemWr);
  or or_8 (ExtOp[0], U_type_out, BandJ[2]);
  or or_9 (ExtOp[1], BandJ[2], MemWr);
  or or_10 (MemOp[0], lb_out, lbu_out, sb_out);
  or or_11 (MemOp[1], lh_out, lhu_out, sh_out);
  or or_12 (MemOp[2], lb_out, lh_out, sb_out, sh_out);
  and lui (lui_out, opcode[5], U_type_out);
  or or_13 (ALUctr[0], lui_out, and_out, andi_out, sra_out, srai_out, sltu_out, sltiu_out, srl_out, srli_out, sll_out, slli_out, blt_ge_u_out);
  or or_14 (ALUctr[1], lui_out, and_out, andi_out, sltu_out, sltiu_out, slt_out, slti_out, or_out, ori_out, BandJ[2]);
  or or_15 (ALUctr[2], lui_out, srl_out, srli_out, and_out, andi_out, sra_out, srai_out, or_out, ori_out, xor_out, xori_out);
  or or_16 (ALUctr[3], lui_out, sra_out, srai_out, sub_out);

  // Notes on the sheet:
  //   输入引脚
  //   请勿修改引脚名称、电路名称及电路封装外观
  //   提示：根据指令种类，把7位指令code用一位指令类型标志位来表示，再通过功能码来区分具体指令，生成控制信号。
  //   输出引脚
endmodule
